// Logisim project cpu.circ as structural Verilog: 1 circuit, main circuit cpu
module cpu (
  input  clk,
  input  [31:0] INSTRUCTION,
  input  [31:0] READ_DATA,
  output [31:0] WRITE_ADDRESS,
  output [31:0] PROGRAM_COUNTER,
  output [31:0] ra,
  output [31:0] sp,
  output [31:0] t0,
  output [31:0] t1,
  output [31:0] t2,
  output [31:0] s0,
  output [31:0] s1,
  output [31:0] a0,
  output [31:0] tohost,
  output [3:0] WRITE_ENABLE,
  output [31:0] WRITE_DATA,
  output [31:0] out_17,
  output [31:0] out_18,
  output out_19,
  output [31:0] out_20,
  output [31:0] out_21,
  output [1:0] out_22,
  output out_23,
  output out_24
);

  wire ASel, BrEq, BrLt, BrUn, CSRSel, CSRWen, RegWEn;
  wire [2:0] ImmSel;
  wire [3:0] ALUSel, multiplexer_6_out, shifter_1_out;
  wire [31:0] adder_1_out, ALU_a, bit_extender_1_out, INSTRUCTION_pipeline, multiplexer_1_out,
       multiplexer_2_out, multiplexer_3_out, multiplexer_5_out, PC_4, PROGRAM_COUNTER_pipeline, Read_Data_1;

  Register #(.width(32)) PC (.D(multiplexer_1_out), .clk(clk), .Q(PROGRAM_COUNTER));  // open: en, clr
  Multiplexer #(.enable("false"), .width(32)) multiplexer_1 (
    .in0(adder_1_out), .in1(out_21), .out(multiplexer_1_out), .sel(out_19));
  Register #(.width(32)) pc_pipe_reg (.D(PROGRAM_COUNTER), .clk(clk), .Q(PROGRAM_COUNTER_pipeline));  // open: en, clr
  Register #(.width(32)) inst_pipe_reg (.D(multiplexer_2_out), .clk(clk), .Q(INSTRUCTION_pipeline));  // open: en, clr
  Multiplexer #(.enable("false"), .width(32)) multiplexer_2 (
    .in0(INSTRUCTION), .in1(32'h13), .out(multiplexer_2_out), .sel(out_19));
  Adder #(.width(32)) adder_1 (.a(PROGRAM_COUNTER), .b(32'h4), .out(adder_1_out));  // open: cin, cout
  regfile regfile_1 (
    .rs1(INSTRUCTION_pipeline[19:15]), .rs2(INSTRUCTION_pipeline[24:20]), .rd(INSTRUCTION_pipeline[11:7]),
    .Write_Data(out_18), .RegWEn(RegWEn), .clk(clk), .ra(ra), .sp(sp), .t0(t0), .t1(t1), .t2(t2), .s0(s0),
    .s1(s1), .a0(a0), .Read_Data_1(Read_Data_1), .Read_Data_2(out_17));
  imm_gen imm_gen_1 (.inst(INSTRUCTION_pipeline), .ImmSel(ImmSel), .imm(out_20));
  Multiplexer #(.enable("false"), .width(32)) multiplexer_3 (
    .in0(Read_Data_1), .in1(bit_extender_1_out), .out(multiplexer_3_out), .sel(CSRSel));
  assign bit_extender_1_out = {{27{1'b0}}, INSTRUCTION_pipeline[19:15]};  // Bit_Extender bit_extender_1
  control_logic control_logic_1 (
    .inst(INSTRUCTION_pipeline), .BrEq(BrEq), .BrLt(BrLt), .PCSel(out_19), .RegWEn(RegWEn), .ImmSel(ImmSel),
    .BrUn(BrUn), .ASel(ASel), .BSel(out_24), .ALUSel(ALUSel), .MemRW(out_23), .WBSel(out_22),
    .CSRSel(CSRSel), .CSRWen(CSRWen));  // open: out_15, out_16
  branch_comp branch_comp_1 (.rs1(Read_Data_1), .rs2(out_17), .BrUn(BrUn), .BrEq(BrEq), .BrLt(BrLt));
  Multiplexer #(.enable("false"), .width(32)) multiplexer_4 (
    .in0(Read_Data_1), .in1(PROGRAM_COUNTER_pipeline), .out(ALU_a), .sel(ASel));
  // csr csr_1: pin names not known; wires that end beside it: INSTRUCTION_pipeline[31:20], multiplexer_3_out, CSRWen, clk, tohost
  Multiplexer #(.enable("false"), .width(32)) multiplexer_5 (
    .in0(out_17), .in1(out_20), .out(multiplexer_5_out), .sel(out_24));
  alu alu_1 (.Result(out_21), .A(ALU_a), .B(multiplexer_5_out), .ALUSel(ALUSel));
  Multiplexer #(.enable("false"), .select(2), .width(4)) multiplexer_6 (
    .in0(4'b0001), .in1(4'b0011), .in2(4'b1111), .out(multiplexer_6_out), .sel(INSTRUCTION_pipeline[13:12]));  // open: in3
  Adder #(.width(32)) adder_2 (.a(PROGRAM_COUNTER_pipeline), .b(32'h4), .out(PC_4));  // open: cin, cout
  Shifter #(.width(4)) shifter_1 (.in(multiplexer_6_out), .\dist (out_20[1:0]), .out(shifter_1_out));
  Multiplexer #(.enable("false"), .width(4)) multiplexer_7 (
    .in0(4'b0000), .in1(shifter_1_out), .out(WRITE_ENABLE), .sel(out_23));
  Multiplexer #(.enable("false"), .select(2), .width(32)) multiplexer_8 (
    .in0(PC_4), .in1(out_21), .in2(READ_DATA), .out(out_18), .sel(out_22));  // open: in3

  assign WRITE_ADDRESS = out_21;
  assign WRITE_DATA = out_17;

  // Other names for the same wires on the sheet: ALU_out[31:0] = out_21; BSel = out_24; Imm_res[31:0] = out_20;
  //   shift_sel = INSTRUCTION[5]; MemRW = out_23; PCSel = out_19; Read_Data_2[31:0] = out_17; WB[31:0] = out_18;
  //   WBSel[1:0] = out_22

  // Notes on the sheet:
  //   Output to IMEM
  //   IMEM (do **NOT** move this)
  //   Inputs from IMEM
  //   It is OK to move the PC, RegFile, ALU, MEM, Branch Comp, Imm Gen, and Control Logic to wherever is most convenient for you when constructing your CPU, and to delete this text
  //   Inputs/Outputs for testing. Do **NOT** move these.
  //   Outputs To DMEM
  //   DMEM (do **NOT** move this)
  //   Inputs From DMEM
endmodule
