// Logisim project imm-gen.circ as structural Verilog: 1 circuit, main circuit imm_gen
module imm_gen (
  input  [31:0] inst,
  input  [2:0] ImmSel,
  output [31:0] imm
);

  wire [31:0] B, bit_extender_4_out, I, J, J_type_afd1fc15, S, U;

  assign I = {{20{inst[31]}}, inst[31:20]};  // Bit_Extender bit_extender_1
  assign S = {{20{inst[31]}}, {inst[31:25], inst[11:7]}};  // Bit_Extender bit_extender_2
  assign B = {{20{inst[31]}}, {inst[31:25], inst[11:8], 1'b0}};  // Bit_Extender bit_extender_3
  assign bit_extender_4_out = {{12{inst[31]}}, inst[31:12]};  // Bit_Extender bit_extender_4
  Shifter #(.width(32)) shifter_1 (.in(bit_extender_4_out), .\dist (5'b01100), .out(U));
  Multiplexer #(.enable("false"), .select(3), .width(32)) multiplexer_1 (
    .in0(I), .in1(S), .in2(B), .in3(U), .in4(J), .out(imm), .sel(ImmSel));  // open: in5, in6, in7
  assign J_type_afd1fc15 = {{11{inst[31]}}, {inst[31], inst[19:12], inst[20], inst[30:21], 1'b0}};  // Bit_Extender bit_extender_5

  // Other names for the same wires on the sheet: B20_24[4:0] = inst[24:20]; B25_30[5:0] = inst[30:25];
  //   B12_14[2:0] = inst[14:12]; B15_19[4:0] = inst[19:15]; B31 = inst[31]; B7 = inst[7]; B8_11[3:0] = inst[11:8]

  // Notes on the sheet:
  //   INPUTS to your circuit
  //   DON'T CHANGE THE LOCATIONS OF THE INPUTS AND OUTPUTS!
  //   OUTPUT from your circuit
endmodule
